// Digital circuit hw1_4bit_adder.dig as structural Verilog
module hw1_4bit_adder (
  input  A0,
  input  B0,
  input  Cin,
  input  A1,
  input  B1,
  input  A2,
  input  B2,
  input  A3,
  input  B3,
  output Cout,
  output S1,
  output Cout_2,
  output S2,
  output Cout_3,
  output S3,
  output Cout_4,
  output S0
);

  wire and_1_out, and_2_out, and_3_out, and_4_out, and_5_out, and_6_out, and_7_out, and_8_out, xor_1_out,
       xor_2_out, xor_5_out, xor_6_out;

  and and_1 (and_1_out, A0, B0);
  and and_2 (and_2_out, xor_1_out, Cin);
  and and_3 (and_3_out, A2, B2);
  and and_4 (and_4_out, xor_2_out, Cout_2);
  xor xor_1 (xor_1_out, A0, B0);
  xor xor_2 (xor_2_out, A2, B2);
  xor xor_3 (S0, xor_1_out, Cin);
  xor xor_4 (S2, xor_2_out, Cout_2);
  or or_1 (Cout, and_1_out, and_2_out);
  or or_2 (Cout_3, and_3_out, and_4_out);
  xor xor_5 (xor_5_out, A1, B1);
  and and_5 (and_5_out, A1, B1);
  and and_6 (and_6_out, xor_5_out, Cout);
  xor xor_6 (xor_6_out, A3, B3);
  and and_7 (and_7_out, A3, B3);
  and and_8 (and_8_out, xor_6_out, Cout_3);
  xor xor_7 (S1, xor_5_out, Cout);
  xor xor_8 (S3, xor_6_out, Cout_3);
  or or_3 (Cout_2, and_5_out, and_6_out);
  or or_4 (Cout_4, and_7_out, and_8_out);
endmodule
